// Logisim project alu.circ as structural Verilog: 1 circuit, main circuit alu
module alu (
  input  [31:0] A,
  input  [31:0] B,
  input  [3:0] ALUSel,
  output [31:0] Result,
  output [31:0] out_5
);

  wire comparator_1_lt;
  wire [31:0] A_B, A_B_inv, A_inv_B, A_inv_B_inv, add0, and1, B_inv, div8, mul10, mulh14, mulhu11,
       multiplier_4_cout, multiplier_5_cout, not_1_out, not_2_out, or2, remu9, sll6, slt7, sra5, srl4, sub12,
       xor3;

  Multiplexer #(.select(4), .width(32), .enable("false")) multiplexer_1 (
    .in0(add0), .in1(and1), .in2(or2), .in3(xor3), .in4(srl4), .in5(sra5), .in6(sll6), .in7(slt7),
    .in8(div8), .in9(remu9), .in10(mul10), .in11(mulhu11), .in12(sub12), .in13(B), .in14(mulh14),
    .out(Result), .sel(ALUSel));  // open: in15
  Adder #(.width(32)) adder_1 (.a(A), .b(B), .out(add0));  // open: cin, cout
  assign and1 = A & B;  // AND_Gate and_1, 32 bits wide
  assign or2 = A | B;  // OR_Gate or_1, 32 bits wide
  assign xor3 = A ^ B;  // XOR_Gate xor_1, 32 bits wide
  Shifter #(.width(32), .shift("lr")) shifter_1 (.in(A), .\dist (B[4:0]), .out(srl4));
  Shifter #(.width(32), .shift("ar")) shifter_2 (.in(A), .\dist (B[4:0]), .out(sra5));
  Shifter #(.width(32)) shifter_3 (.in(A), .\dist (B[4:0]), .out(sll6));
  Comparator #(.width(32)) comparator_1 (.a(A), .b(B), .lt(comparator_1_lt));  // open: gt, eq
  Divider #(.width(32)) divider_1 (.a(A), .b(B), .out(div8));  // open: upper, rem
  Divider #(.width(32)) divider_2 (.a(A), .b(B), .rem(remu9));  // open: out, upper
  Multiplier #(.width(32)) multiplier_1 (.a(A), .b(B), .out(mul10));  // open: cin, cout
  Multiplier #(.width(32)) multiplier_2 (.a(A), .b(B), .cout(mulhu11));  // open: out, cin
  Subtractor #(.width(32)) subtractor_1 (.a(A), .b(B), .out(sub12));  // open: bin, bout
  assign slt7 = {{31{1'b0}}, comparator_1_lt};  // Bit_Extender bit_extender_1
  Multiplexer #(.select(2), .width(32), .enable("false")) multiplexer_2 (
    .in0(A_B), .in1(A_B_inv), .in2(A_inv_B), .in3(A_inv_B_inv), .out(mulh14), .sel({A[31], B[31]}));
  assign not_1_out = ~A;  // NOT_Gate not_1, 32 bits wide
  assign not_2_out = ~B;  // NOT_Gate not_2, 32 bits wide
  Multiplier #(.width(32)) multiplier_3 (.a(A), .b(B), .cout(A_B));  // open: out, cin
  Multiplier #(.width(32)) multiplier_4 (.a(out_5), .b(B), .cout(multiplier_4_cout));  // open: out, cin
  Multiplier #(.width(32)) multiplier_5 (.a(A), .b(B_inv), .cout(multiplier_5_cout));  // open: out, cin
  Multiplier #(.width(32)) multiplier_6 (.a(out_5), .b(B_inv), .cout(A_inv_B_inv));  // open: out, cin
  Adder #(.width(32)) adder_2 (.a(not_1_out), .b(32'h1), .out(out_5));  // open: cin, cout
  Adder #(.width(32)) adder_3 (.a(not_2_out), .b(32'h1), .out(B_inv));  // open: cin, cout
  assign A_inv_B = ~multiplier_4_cout;  // NOT_Gate not_3, 32 bits wide
  assign A_B_inv = ~multiplier_5_cout;  // NOT_Gate not_4, 32 bits wide

  // Other names for the same wires on the sheet: A_inv[31:0] = out_5

  // Notes on the sheet:
  //   INPUTS to your circuit
  //   DON'T CHANGE THE LOCATIONS OF THE INPUTS AND OUTPUTS!
  //   OUTPUT from your circuit
endmodule
