// Logisim project alu_temp.circ as structural Verilog: 1 circuit, main circuit main
module main (
  input  [6:0] in_1,
  input  [2:0] in_2,
  input  [6:0] in_3,
  output [3:0] out_4
);

  wire and_1_out, and_3_out, and_4_out, and_5_out, and_6_out, and_8_out, and_9_out, and_10_out, and_13_out,
       and_16_out, and_18_out, and_27_out, and_28_out, and_29_out, and_30_out, and_31_out, and_32_out,
       comparator_1_eq, comparator_2_eq, comparator_3_eq, comparator_4_eq, comparator_5_eq, comparator_6_eq,
       comparator_7_eq, comparator_8_eq, comparator_20_gt, f3_0x0, f3_0x1, f3_0x2, f3_0x3, f3_0x4, f3_0x5,
       f3_0x6, f3_0x7, f7_0x00, f7_0x01, f7_0x20, is_add, is_addi, is_and, is_andi, is_B_type, is_divu,
       is_I_arith_ins, is_I_jalr_ins, is_I_load_ins, is_J_type, is_mul, is_mulh, is_mulhu, is_or, is_ori,
       is_R_type, is_remu, is_S_type, is_sll, is_slli, is_slt, is_slti, is_srai, is_srl, is_srli, is_sub,
       is_U_type, is_xor, is_xori, or_1_out, or_2_out, or_3_out, or_4_out, or_5_out;
  wire [3:0] alu_sel;

  Multiplexer #(.enable("false")) multiplexer_1 (.in0(1'b0), .in1(1'b1), .out(is_R_type), .sel(comparator_1_eq));
  Comparator #(.width(7)) comparator_1 (.a(in_1), .b(7'b0110011), .eq(comparator_1_eq));  // open: gt, lt
  Multiplexer #(.enable("false")) multiplexer_2 (.in0(1'b0), .in1(1'b1), .out(is_I_load_ins), .sel(comparator_2_eq));
  Comparator #(.width(7)) comparator_2 (.a(in_1), .b(7'b0000011), .eq(comparator_2_eq));  // open: gt, lt
  Multiplexer #(.enable("false")) multiplexer_3 (.in0(1'b0), .in1(1'b1), .out(is_I_arith_ins), .sel(comparator_3_eq));
  Comparator #(.width(7)) comparator_3 (.a(in_1), .b(7'b0010011), .eq(comparator_3_eq));  // open: gt, lt
  Multiplexer #(.enable("false")) multiplexer_4 (.in0(1'b0), .in1(1'b1), .out(is_I_jalr_ins), .sel(comparator_4_eq));
  Comparator #(.width(7)) comparator_4 (.a(in_1), .b(7'b1100111), .eq(comparator_4_eq));  // open: gt, lt
  Multiplexer #(.enable("false")) multiplexer_5 (.in0(1'b0), .in1(1'b1), .out(is_S_type), .sel(comparator_5_eq));
  Comparator #(.width(7)) comparator_5 (.a(in_1), .b(7'b0100011), .eq(comparator_5_eq));  // open: gt, lt
  Multiplexer #(.enable("false")) multiplexer_6 (.in0(1'b0), .in1(1'b1), .out(is_B_type), .sel(comparator_6_eq));
  Comparator #(.width(7)) comparator_6 (.a(in_1), .b(7'b1100011), .eq(comparator_6_eq));  // open: gt, lt
  Multiplexer #(.enable("false")) multiplexer_7 (.in0(1'b0), .in1(1'b1), .out(is_U_type), .sel(comparator_7_eq));
  Comparator #(.width(7)) comparator_7 (.a(in_1), .b(7'b0110111), .eq(comparator_7_eq));  // open: gt, lt
  Multiplexer #(.enable("false")) multiplexer_8 (.in0(1'b0), .in1(1'b1), .out(is_J_type), .sel(comparator_8_eq));
  Comparator #(.width(7)) comparator_8 (.a(in_1), .b(7'b1101111), .eq(comparator_8_eq));  // open: gt, lt
  Comparator #(.width(3)) comparator_9 (.a(in_2), .b(3'b000), .eq(f3_0x0));  // open: gt, lt
  Comparator #(.width(3)) comparator_10 (.a(in_2), .b(3'b001), .eq(f3_0x1));  // open: gt, lt
  Comparator #(.width(3)) comparator_11 (.a(in_2), .b(3'b010), .eq(f3_0x2));  // open: gt, lt
  Comparator #(.width(3)) comparator_12 (.a(in_2), .b(3'b011), .eq(f3_0x3));  // open: gt, lt
  Comparator #(.width(3)) comparator_13 (.a(in_2), .b(3'b100), .eq(f3_0x4));  // open: gt, lt
  Comparator #(.width(3)) comparator_14 (.a(in_2), .b(3'b101), .eq(f3_0x5));  // open: gt, lt
  Comparator #(.width(3)) comparator_15 (.a(in_2), .b(3'b110), .eq(f3_0x6));  // open: gt, lt
  Comparator #(.width(3)) comparator_16 (.a(in_2), .b(3'b111), .eq(f3_0x7));  // open: gt, lt
  Comparator #(.width(7)) comparator_17 (.a(in_3), .b({7{1'b0}}), .eq(f7_0x00));  // open: gt, lt
  Comparator #(.width(7)) comparator_18 (.a(in_3), .b(7'b0000001), .eq(f7_0x01));  // open: gt, lt
  Comparator #(.width(7)) comparator_19 (.a(in_3), .b(7'b0100000), .eq(f7_0x20));  // open: gt, lt
  and and_1 (and_1_out, is_R_type, f3_0x4);
  and and_2 (is_xori, is_I_arith_ins, f3_0x4);
  and and_3 (and_3_out, is_R_type, f3_0x5);
  and and_4 (and_4_out, is_I_arith_ins, f3_0x5);
  and and_5 (and_5_out, is_R_type, f3_0x1);
  and and_6 (and_6_out, is_R_type, f3_0x2);
  and and_7 (is_slti, is_I_arith_ins, f3_0x2);
  and and_8 (and_8_out, is_R_type, f3_0x5);
  and and_9 (and_9_out, is_R_type, f3_0x7);
  and and_10 (and_10_out, is_R_type, f3_0x0);
  and and_11 (is_add, and_10_out, f7_0x00);
  and and_12 (is_addi, is_I_arith_ins, f3_0x0);
  and and_13 (and_13_out, is_R_type, f3_0x7);
  and and_14 (is_and, and_13_out, f7_0x00);
  and and_15 (is_andi, is_I_arith_ins, f3_0x7);
  and and_16 (and_16_out, is_R_type, f3_0x6);
  and and_17 (is_or, and_16_out, f7_0x00);
  and and_18 (and_18_out, is_I_arith_ins, f3_0x6);
  buf and_19 (is_ori, and_18_out);  // AND_Gate
  and and_20 (is_xor, and_1_out, f7_0x00);
  and and_21 (is_srl, and_3_out, f7_0x00);
  and and_22 (is_srai, and_4_out, f7_0x20);
  and and_23 (is_sll, and_5_out, f7_0x00);
  and and_24 (is_slt, and_6_out, f7_0x00);
  and and_25 (is_divu, and_8_out, f7_0x01);
  and and_26 (is_remu, and_9_out, f7_0x01);
  Multiplexer #(.width(4), .enable("false")) multiplexer_9 (.in1(4'b0000), .out(alu_sel), .sel(or_1_out));  // open: in0
  or or_1 (or_1_out, is_add, is_addi);
  Multiplexer #(.width(4), .enable("false")) multiplexer_10 (
    .in1(4'b0001), .out(alu_sel), .sel(or_2_out));  // open: in0
  or or_2 (or_2_out, is_and, is_andi);
  Multiplexer #(.width(4), .enable("false")) multiplexer_11 (
    .in1(4'b0010), .out(alu_sel), .sel(or_3_out));  // open: in0
  or or_3 (or_3_out, is_or, is_ori);
  Multiplexer #(.width(4), .enable("false")) multiplexer_12 (
    .in1(4'b0011), .out(alu_sel), .sel(or_4_out));  // open: in0
  or or_4 (or_4_out, is_xor, is_xori);
  Multiplexer #(.width(4), .enable("false")) multiplexer_13 (.in1(4'b0100), .out(alu_sel), .sel(is_srl));  // open: in0
  Multiplexer #(.width(4), .enable("false")) multiplexer_14 (.in1(4'b0101), .out(alu_sel), .sel(is_srai));  // open: in0
  Multiplexer #(.width(4), .enable("false")) multiplexer_15 (.in1(4'b0110), .out(alu_sel), .sel(is_sll));  // open: in0
  Multiplexer #(.width(4), .enable("false")) multiplexer_16 (
    .in1(4'b0111), .out(alu_sel), .sel(or_5_out));  // open: in0
  or or_5 (or_5_out, is_slt, is_slti);
  Multiplexer #(.width(4), .enable("false")) multiplexer_17 (.in1(4'b1000), .out(alu_sel), .sel(is_divu));  // open: in0
  Multiplexer #(.width(4), .enable("false")) multiplexer_18 (.in1(4'b1001), .out(alu_sel), .sel(is_remu));  // open: in0
  and and_27 (and_27_out, is_I_arith_ins, f3_0x5);
  and and_28 (and_28_out, is_I_arith_ins, f3_0x1);
  Multiplexer #(.width(4), .enable("false")) multiplexer_19 (
    .in0(4'b0000), .in1(alu_sel), .out(out_4), .sel(comparator_20_gt));
  Comparator #(.width(4), .mode("unsigned")) comparator_20 (
    .a(alu_sel), .b(4'b0000), .gt(comparator_20_gt));  // open: eq, lt
  and and_29 (and_29_out, is_R_type, f3_0x0);
  and and_30 (and_30_out, is_R_type, f3_0x3);
  and and_31 (and_31_out, is_R_type, f3_0x0);
  and and_32 (and_32_out, is_R_type, f3_0x1);
  and and_33 (is_srli, and_27_out, f7_0x00);
  and and_34 (is_slli, and_28_out, f7_0x00);
  and and_35 (is_mul, and_29_out, f7_0x01);
  and and_36 (is_mulhu, and_30_out, f7_0x01);
  and and_37 (is_sub, and_31_out, f7_0x20);
  and and_38 (is_mulh, and_32_out, f7_0x01);
  Multiplexer #(.width(4), .enable("false")) multiplexer_20 (.in1(4'b0110), .out(alu_sel), .sel(is_slli));  // open: in0
  Multiplexer #(.width(4), .enable("false")) multiplexer_21 (
    .in1(4'b1011), .out(alu_sel), .sel(is_mulhu));  // open: in0
  Multiplexer #(.width(4), .enable("false")) multiplexer_22 (.in1(4'b1110), .out(alu_sel), .sel(is_mulh));  // open: in0
  Multiplexer #(.width(4), .enable("false")) multiplexer_23 (.in1(4'b0100), .out(alu_sel), .sel(is_srli));  // open: in0
  Multiplexer #(.width(4), .enable("false")) multiplexer_24 (.in1(4'b1010), .out(alu_sel), .sel(is_mul));  // open: in0
  Multiplexer #(.width(4), .enable("false")) multiplexer_25 (.in1(4'b1100), .out(alu_sel), .sel(is_sub));  // open: in0

  // Other names for the same wires on the sheet: func3[2:0] = in_2; func7[6:0] = in_3; opcode[6:0] = in_1

  // Notes on the sheet:
  //   R-type
  //   I-type
  //   S-type
  //   B-type
  //   U-type
  //   J-type
  //   func3 possible values
  //   func7 possible values
  //   xor operation
  //   srl operation
  //   srai operation
  //   sll operation
  //   slt operation
  //   divu operation
  //   remu operation
  //   add operation
  //   and operation
  //   or operation
  //   beq, blt, bltu, bne, jal, jalr
  //   MIGHT NOT NEED
  //   srli operation
  //   slli operation
  //   mul operation
  //   mulhu operation
  //   sub operation
  //   mulh operation
endmodule
