// Logisim project cpu.circ as structural Verilog: 10 circuits, main circuit main
module main (
  input  [31:0] INSTRUCTION,
  input  CLOCK,
  output [31:0] PROGRAM_COUNTER,
  output [31:0] ra,
  output [31:0] sp,
  output [31:0] t0,
  output [31:0] t1,
  output [31:0] t2,
  output [31:0] s0,
  output [31:0] s1,
  output [31:0] a0
);

  wire ASel, BSel, currNOPSel, DMEM_p4, MemRW, NOPSel, PCSel, rd_valid, rs1_valid, rs2_valid;
  wire [1:0] WBSel;
  wire [2:0] func3;
  wire [3:0] ALUSel;
  wire [4:0] multiplexer_1_out, rd, rs1, rs2;
  wire [6:0] func7, opcode;
  wire [31:0] adder_1_out, ALU_output, Immediate, multiplexer_2_out, multiplexer_3_out, multiplexer_4_out,
       multiplexer_5_out, old_PC, parsed_read_data, read_data, register_1_q, rs1_data, rs2_data, write_data;

  Register #(.width(32)) register_1 (.D(INSTRUCTION), .clk(CLOCK), .Q(register_1_q));  // open: en, clr
  Multiplexer #(.width(5), .enable("false")) multiplexer_1 (
    .in0({5{1'b0}}), .in1(rs1), .out(multiplexer_1_out), .sel(rs1_valid));
  Register #(.width(1)) register_2 (.D(NOPSel), .clk(CLOCK), .Q(currNOPSel));  // open: en, clr
  Multiplexer #(.width(32), .enable("false")) multiplexer_2 (
    .in0(register_1_q), .in1(32'h13), .out(multiplexer_2_out), .sel(currNOPSel));
  instruction_decode instruction_decode_1 (
    .in_1(multiplexer_2_out), .opcode(opcode), .func3(func3), .func7(func7), .rd(rd), .rs1(rs1), .rs2(rs2),
    .rs2_valid(rs2_valid), .rd_valid(rd_valid), .immediate(Immediate), .rs1_valid(rs1_valid));  // open: func3_valid, func7_valid
  regfile_main RegFile (
    .rs2(rs2), .rd(rd), .Read_Data_1(rs1_data), .Read_Data_2(rs2_data), .ra(ra), .sp(sp), .t0(t0), .t1(t1),
    .t2(t2), .s0(s0), .s1(s1), .a0(a0), .rs1(multiplexer_1_out), .Write_Data(write_data), .RegWEn(rd_valid),
    .clk(CLOCK));
  wb_sel wb_sel_1 (.opcode(opcode), .WBSel(WBSel));
  alu_sel alu_sel_1 (.opcode(opcode), .func3(func3), .func7(func7), .ALUSel(ALUSel));
  pc_selector pc_selector_1 (.rs1_data(rs1_data), .rs2_data(rs2_data), .opcode(opcode), .func3(func3), .PCSel(PCSel));
  b_sel b_sel_1 (.opcode(opcode), .rs2_valid(rs2_valid), .MemRW(MemRW), .BSel(BSel));
  a_sel a_sel_1 (.opcode(opcode), .ASel(ASel));
  nop_sel nop_sel_1 (.opcode(opcode), .PCSel(PCSel), .NOPSel(NOPSel));
  load_parse load_parse_1 (.read_data(read_data), .opcode(opcode), .func3(func3), .load_output(parsed_read_data));
  Adder #(.width(32)) adder_1 (.a(PROGRAM_COUNTER), .b(32'h4), .out(adder_1_out));  // open: cin, cout
  Multiplexer #(.width(32), .enable("false")) multiplexer_3 (
    .in0(rs1_data), .in1(old_PC), .out(multiplexer_3_out), .sel(ASel));
  Multiplexer #(.width(32), .enable("false")) multiplexer_4 (
    .in0(Immediate), .in1(rs2_data), .out(multiplexer_4_out), .sel(BSel));
  Multiplexer #(.width(32), .enable("false")) multiplexer_5 (
    .in0(adder_1_out), .in1(ALU_output), .out(multiplexer_5_out), .sel(PCSel));
  alu alu_1 (.ALUSel(ALUSel), .B(multiplexer_4_out), .A(multiplexer_3_out), .Result(ALU_output));  // open: out_5
  Register #(.width(32)) PC (.D(multiplexer_5_out), .clk(CLOCK), .Q(PROGRAM_COUNTER));  // open: en, clr
  Multiplexer #(.select(2), .width(32), .enable("false")) multiplexer_6 (
    .in0(rs2_data), .in1(ALU_output), .in2(parsed_read_data), .in3(PROGRAM_COUNTER), .out(write_data),
    .sel(WBSel));
  Register #(.width(32)) register_3 (.D(PROGRAM_COUNTER), .en(DMEM_p4), .clk(CLOCK), .Q(old_PC));  // open: clr
  // mem_main DMEM: pin names not known; wires that end beside it: ALU_output, write_data, CLOCK, DMEM_p4, MemRW, read_data

  // Other names for the same wires on the sheet: clk = CLOCK

  // Notes on the sheet:
  //   Output
  //   IMEM (do **NOT** move this)
  //   Inputs
  //   Inputs/Outputs for testing. Do **NOT** move these.
endmodule

module instruction_decode (
  input  [31:0] in_1,
  output [6:0] opcode,
  output [2:0] func3,
  output [6:0] func7,
  output [4:0] rd,
  output [4:0] rs1,
  output [4:0] rs2,
  output rs2_valid,
  output rd_valid,
  output [31:0] immediate,
  output rs1_valid,
  output func3_valid,
  output func7_valid
);

  wire [2:0] opcode_parse_1_out_2, opcode_parse_2_out_2, opcode_parse_3_out_2, opcode_parse_4_out_2,
       opcode_parse_5_out_2, opcode_parse_6_out_2;
  wire [31:0] bit_extender_1_out, bit_extender_2_out, bit_extender_3_out, bit_extender_4_out;

  Multiplexer #(.select(3), .enable("false")) multiplexer_1 (
    .in0(1'b1), .in1(1'b0), .in2(1'b1), .in3(1'b1), .in4(1'b0), .in5(1'b0), .out(rs2_valid),
    .sel(opcode_parse_1_out_2));  // open: in6, in7
  opcode_parse opcode_parse_1 (.in_1(in_1[6:0]), .out_2(opcode_parse_1_out_2));
  Multiplexer #(.select(3), .enable("false")) multiplexer_2 (
    .in0(1'b1), .in1(1'b1), .in2(1'b1), .in3(1'b1), .in4(1'b0), .in5(1'b0), .out(rs1_valid),
    .sel(opcode_parse_2_out_2));  // open: in6, in7
  opcode_parse opcode_parse_2 (.in_1(in_1[6:0]), .out_2(opcode_parse_2_out_2));
  Multiplexer #(.select(3), .enable("false")) multiplexer_3 (
    .in0(1'b1), .in1(1'b0), .in2(1'b0), .in3(1'b0), .in4(1'b0), .in5(1'b0), .out(func7_valid),
    .sel(opcode_parse_3_out_2));  // open: in6, in7
  opcode_parse opcode_parse_3 (.in_1(in_1[6:0]), .out_2(opcode_parse_3_out_2));
  Multiplexer #(.select(3), .enable("false")) multiplexer_4 (
    .in0(1'b1), .in1(1'b1), .in2(1'b0), .in3(1'b0), .in4(1'b1), .in5(1'b1), .out(rd_valid),
    .sel(opcode_parse_4_out_2));  // open: in6, in7
  opcode_parse opcode_parse_4 (.in_1(in_1[6:0]), .out_2(opcode_parse_4_out_2));
  Multiplexer #(.select(3), .enable("false")) multiplexer_5 (
    .in0(1'b1), .in1(1'b1), .in2(1'b1), .in3(1'b1), .in4(1'b0), .in5(1'b0), .out(func3_valid),
    .sel(opcode_parse_5_out_2));  // open: in6, in7
  opcode_parse opcode_parse_5 (.in_1(in_1[6:0]), .out_2(opcode_parse_5_out_2));
  assign bit_extender_1_out = {{20{in_1[31]}}, in_1[31:20]};  // Bit_Extender bit_extender_1
  assign bit_extender_2_out = {{20{in_1[31]}}, {in_1[31:25], in_1[11:7]}};  // Bit_Extender bit_extender_2
  assign bit_extender_3_out = {{19{in_1[31]}}, {in_1[31], in_1[7], in_1[30:25], in_1[11:8], 1'b0}};  // Bit_Extender bit_extender_3
  assign bit_extender_4_out = {{11{in_1[31]}}, {in_1[31], in_1[19:12], in_1[20], in_1[30:21], 1'b0}};  // Bit_Extender bit_extender_4
  opcode_parse opcode_parse_6 (.in_1(in_1[6:0]), .out_2(opcode_parse_6_out_2));
  Multiplexer #(.select(3), .width(32), .enable("false")) multiplexer_6 (
    .in1(bit_extender_1_out), .in2(bit_extender_2_out), .in3(bit_extender_3_out),
    .in4({in_1[31:12], {12{1'b0}}}), .in5(bit_extender_4_out), .out(immediate), .sel(opcode_parse_6_out_2));  // open: in0, in6, in7

  assign func3 = in_1[14:12];
  assign func7 = in_1[31:25];
  assign opcode = in_1[6:0];
  assign rd = in_1[11:7];
  assign rs1 = in_1[19:15];
  assign rs2 = in_1[24:20];

  // Other names for the same wires on the sheet: Imm_11_0_I_type[11:0] = in_1[31:20];
  //   Imm_20_1_J_type[19:0] = {in_1[31], in_1[19:12], in_1[20], in_1[30:21]}; Imm_31_12_U_type[19:0] = in_1[31:12];
  //   instruction_in[31:0] = in_1; func7_t[6:0] = in_1[31:25]; Imm_11_0_S_type[11:0] = {in_1[31:25], in_1[11:7]};
  //   Imm_12_1_B_type[11:0] = {in_1[31], in_1[7], in_1[30:25], in_1[11:8]}; func3_t[2:0] = in_1[14:12];
  //   opcode_t[6:0] = in_1[6:0]
endmodule

module opcode_parse (
  input  [6:0] in_1,
  output [2:0] out_2
);

  wire comparator_1_eq, comparator_2_eq, comparator_3_eq, comparator_4_eq, comparator_5_eq, comparator_6_eq,
       comparator_7_eq, comparator_8_eq;
  wire [2:0] multiplexer_1_out, multiplexer_2_out, multiplexer_3_out, multiplexer_4_out, multiplexer_5_out,
       multiplexer_6_out, multiplexer_7_out;

  Multiplexer #(.width(3), .enable("false")) multiplexer_1 (
    .in0(3'b110), .in1(3'b000), .out(multiplexer_1_out), .sel(comparator_1_eq));
  Comparator #(.width(7)) comparator_1 (.a(in_1), .b(7'b0110011), .eq(comparator_1_eq));  // open: gt, lt
  Comparator #(.width(7)) comparator_2 (.a(in_1), .b(7'b0000011), .eq(comparator_2_eq));  // open: gt, lt
  Multiplexer #(.width(3), .enable("false")) multiplexer_2 (
    .in0(multiplexer_1_out), .in1(3'b001), .out(multiplexer_2_out), .sel(comparator_2_eq));
  Comparator #(.width(7)) comparator_3 (.a(in_1), .b(7'b0010011), .eq(comparator_3_eq));  // open: gt, lt
  Multiplexer #(.width(3), .enable("false")) multiplexer_3 (
    .in0(multiplexer_2_out), .in1(3'b001), .out(multiplexer_3_out), .sel(comparator_3_eq));
  Multiplexer #(.width(3), .enable("false")) multiplexer_4 (
    .in0(multiplexer_3_out), .in1(3'b010), .out(multiplexer_4_out), .sel(comparator_4_eq));
  Comparator #(.width(7)) comparator_4 (.a(in_1), .b(7'b0100011), .eq(comparator_4_eq));  // open: gt, lt
  Multiplexer #(.width(3), .enable("false")) multiplexer_5 (
    .in0(multiplexer_4_out), .in1(3'b011), .out(multiplexer_5_out), .sel(comparator_5_eq));
  Comparator #(.width(7)) comparator_5 (.a(in_1), .b(7'b1100011), .eq(comparator_5_eq));  // open: gt, lt
  Multiplexer #(.width(3), .enable("false")) multiplexer_6 (
    .in0(multiplexer_5_out), .in1(3'b100), .out(multiplexer_6_out), .sel(comparator_6_eq));
  Comparator #(.width(7)) comparator_6 (.a(in_1), .b(7'b0110111), .eq(comparator_6_eq));  // open: gt, lt
  Comparator #(.width(7)) comparator_7 (.a(in_1), .b(7'b1101111), .eq(comparator_7_eq));  // open: gt, lt
  Multiplexer #(.width(3), .enable("false")) multiplexer_7 (
    .in0(multiplexer_6_out), .in1(3'b101), .out(multiplexer_7_out), .sel(comparator_7_eq));
  Multiplexer #(.width(3), .enable("false")) multiplexer_8 (
    .in0(multiplexer_7_out), .in1(3'b001), .out(out_2), .sel(comparator_8_eq));
  Comparator #(.width(7)) comparator_8 (.a(in_1), .b(7'b1100111), .eq(comparator_8_eq));  // open: gt, lt

  // Other names for the same wires on the sheet: opcode[6:0] = in_1

  // Notes on the sheet:
  //   NO OPCODE FOUND
  //   R-type
  //   I-type
  //   I-type
  //   S-type
  //   SB-type
  //   U-type
  //   UJ-type
  //   I-type
endmodule

module pc_selector (
  input  [31:0] rs1_data,
  input  [31:0] rs2_data,
  input  [6:0] opcode,
  input  [2:0] func3,
  output PCSel
);

  wire and_1_out, and_2_out, and_3_out, and_4_out, and_5_out, and_6_out, and_7_out, and_8_out,
       comparator_1_eq, comparator_2_eq, comparator_3_eq, comparator_4_eq, comparator_5_eq, comparator_6_eq,
       comparator_7_eq, comparator_8_eq, comparator_9_eq, comparator_10_eq, equal, less_than_signed,
       less_than_unsigned, not_equal;

  Comparator #(.width(7)) comparator_1 (.a(opcode), .b(7'b1100111), .eq(comparator_1_eq));  // open: gt, lt
  Comparator #(.width(7)) comparator_2 (.a(opcode), .b(7'b1101111), .eq(comparator_2_eq));  // open: gt, lt
  Comparator #(.width(3)) comparator_3 (.a(func3), .b(3'b000), .eq(comparator_3_eq));  // open: gt, lt
  Comparator #(.width(7)) comparator_4 (.a(opcode), .b(7'b1100011), .eq(comparator_4_eq));  // open: gt, lt
  Comparator #(.width(3)) comparator_5 (.a(func3), .b(3'b100), .eq(comparator_5_eq));  // open: gt, lt
  Comparator #(.width(7)) comparator_6 (.a(opcode), .b(7'b1100011), .eq(comparator_6_eq));  // open: gt, lt
  Comparator #(.width(3)) comparator_7 (.a(func3), .b(3'b110), .eq(comparator_7_eq));  // open: gt, lt
  Comparator #(.width(7)) comparator_8 (.a(opcode), .b(7'b1100011), .eq(comparator_8_eq));  // open: gt, lt
  Comparator #(.width(3)) comparator_9 (.a(func3), .b(3'b000), .eq(comparator_9_eq));  // open: gt, lt
  Comparator #(.width(7)) comparator_10 (.a(opcode), .b(7'b1100011), .eq(comparator_10_eq));  // open: gt, lt
  and and_1 (and_1_out, comparator_3_eq, comparator_4_eq);
  and and_2 (and_2_out, comparator_5_eq, comparator_6_eq);
  and and_3 (and_3_out, comparator_7_eq, comparator_8_eq);
  and and_4 (and_4_out, comparator_9_eq, comparator_10_eq);
  Comparator #(.width(32)) comparator_11 (.a(rs1_data), .b(rs2_data), .eq(equal), .lt(less_than_signed));  // open: gt
  Comparator #(.width(32), .mode("unsigned")) comparator_12 (
    .a(rs1_data), .b(rs2_data), .lt(less_than_unsigned));  // open: gt, eq
  and and_5 (and_5_out, equal, and_1_out);
  and and_6 (and_6_out, less_than_signed, and_2_out);
  and and_7 (and_7_out, less_than_unsigned, and_3_out);
  and and_8 (and_8_out, not_equal, and_4_out);
  not not_1 (not_equal, equal);
  or or_1 (PCSel, comparator_1_eq, comparator_2_eq, and_5_out, and_6_out, and_7_out, and_8_out);

  // Other names for the same wires on the sheet: rs1[31:0] = rs1_data; rs2[31:0] = rs2_data
endmodule

module alu_sel (
  input  [6:0] opcode,
  input  [2:0] func3,
  input  [6:0] func7,
  output [3:0] ALUSel
);

  wire and_1_out, and_3_out, and_4_out, and_5_out, and_6_out, and_8_out, and_9_out, and_10_out, and_13_out,
       and_16_out, and_18_out, and_27_out, and_28_out, and_29_out, and_30_out, and_31_out, and_32_out,
       comparator_1_eq, comparator_2_eq, comparator_3_eq, comparator_4_eq, comparator_5_eq, comparator_6_eq,
       comparator_7_eq, comparator_8_eq, comparator_20_gt, f3_0x0, f3_0x1, f3_0x2, f3_0x3, f3_0x4, f3_0x5,
       f3_0x6, f3_0x7, f7_0x00, f7_0x01, f7_0x20, is_add, is_addi, is_and, is_andi, is_B_type, is_divu,
       is_I_arith_ins, is_I_jalr_ins, is_I_load_ins, is_J_type, is_mul, is_mulh, is_mulhu, is_or, is_ori,
       is_R_type, is_remu, is_S_type, is_sll, is_slli, is_slt, is_slti, is_srai, is_srl, is_srli, is_sub,
       is_U_type, is_xor, is_xori, or_1_out, or_2_out, or_3_out, or_4_out, or_5_out;
  wire [3:0] alu_sel;

  Multiplexer #(.enable("false")) multiplexer_1 (.in0(1'b0), .in1(1'b1), .out(is_R_type), .sel(comparator_1_eq));
  Comparator #(.width(7)) comparator_1 (.a(opcode), .b(7'b0110011), .eq(comparator_1_eq));  // open: gt, lt
  Multiplexer #(.enable("false")) multiplexer_2 (.in0(1'b0), .in1(1'b1), .out(is_I_load_ins), .sel(comparator_2_eq));
  Comparator #(.width(7)) comparator_2 (.a(opcode), .b(7'b0000011), .eq(comparator_2_eq));  // open: gt, lt
  Multiplexer #(.enable("false")) multiplexer_3 (.in0(1'b0), .in1(1'b1), .out(is_I_arith_ins), .sel(comparator_3_eq));
  Comparator #(.width(7)) comparator_3 (.a(opcode), .b(7'b0010011), .eq(comparator_3_eq));  // open: gt, lt
  Multiplexer #(.enable("false")) multiplexer_4 (.in0(1'b0), .in1(1'b1), .out(is_I_jalr_ins), .sel(comparator_4_eq));
  Comparator #(.width(7)) comparator_4 (.a(opcode), .b(7'b1100111), .eq(comparator_4_eq));  // open: gt, lt
  Multiplexer #(.enable("false")) multiplexer_5 (.in0(1'b0), .in1(1'b1), .out(is_S_type), .sel(comparator_5_eq));
  Comparator #(.width(7)) comparator_5 (.a(opcode), .b(7'b0100011), .eq(comparator_5_eq));  // open: gt, lt
  Multiplexer #(.enable("false")) multiplexer_6 (.in0(1'b0), .in1(1'b1), .out(is_B_type), .sel(comparator_6_eq));
  Comparator #(.width(7)) comparator_6 (.a(opcode), .b(7'b1100011), .eq(comparator_6_eq));  // open: gt, lt
  Multiplexer #(.enable("false")) multiplexer_7 (.in0(1'b0), .in1(1'b1), .out(is_U_type), .sel(comparator_7_eq));
  Comparator #(.width(7)) comparator_7 (.a(opcode), .b(7'b0110111), .eq(comparator_7_eq));  // open: gt, lt
  Multiplexer #(.enable("false")) multiplexer_8 (.in0(1'b0), .in1(1'b1), .out(is_J_type), .sel(comparator_8_eq));
  Comparator #(.width(7)) comparator_8 (.a(opcode), .b(7'b1101111), .eq(comparator_8_eq));  // open: gt, lt
  Comparator #(.width(3)) comparator_9 (.a(func3), .b(3'b000), .eq(f3_0x0));  // open: gt, lt
  Comparator #(.width(3)) comparator_10 (.a(func3), .b(3'b001), .eq(f3_0x1));  // open: gt, lt
  Comparator #(.width(3)) comparator_11 (.a(func3), .b(3'b010), .eq(f3_0x2));  // open: gt, lt
  Comparator #(.width(3)) comparator_12 (.a(func3), .b(3'b011), .eq(f3_0x3));  // open: gt, lt
  Comparator #(.width(3)) comparator_13 (.a(func3), .b(3'b100), .eq(f3_0x4));  // open: gt, lt
  Comparator #(.width(3)) comparator_14 (.a(func3), .b(3'b101), .eq(f3_0x5));  // open: gt, lt
  Comparator #(.width(3)) comparator_15 (.a(func3), .b(3'b110), .eq(f3_0x6));  // open: gt, lt
  Comparator #(.width(3)) comparator_16 (.a(func3), .b(3'b111), .eq(f3_0x7));  // open: gt, lt
  Comparator #(.width(7)) comparator_17 (.a(func7), .b({7{1'b0}}), .eq(f7_0x00));  // open: gt, lt
  Comparator #(.width(7)) comparator_18 (.a(func7), .b(7'b0000001), .eq(f7_0x01));  // open: gt, lt
  Comparator #(.width(7)) comparator_19 (.a(func7), .b(7'b0100000), .eq(f7_0x20));  // open: gt, lt
  and and_1 (and_1_out, is_R_type, f3_0x4);
  and and_2 (is_xori, is_I_arith_ins, f3_0x4);
  and and_3 (and_3_out, is_R_type, f3_0x5);
  and and_4 (and_4_out, is_I_arith_ins, f3_0x5);
  and and_5 (and_5_out, is_R_type, f3_0x1);
  and and_6 (and_6_out, is_R_type, f3_0x2);
  and and_7 (is_slti, is_I_arith_ins, f3_0x2);
  and and_8 (and_8_out, is_R_type, f3_0x5);
  and and_9 (and_9_out, is_R_type, f3_0x7);
  and and_10 (and_10_out, is_R_type, f3_0x0);
  and and_11 (is_add, and_10_out, f7_0x00);
  and and_12 (is_addi, is_I_arith_ins, f3_0x0);
  and and_13 (and_13_out, is_R_type, f3_0x7);
  and and_14 (is_and, and_13_out, f7_0x00);
  and and_15 (is_andi, is_I_arith_ins, f3_0x7);
  and and_16 (and_16_out, is_R_type, f3_0x6);
  and and_17 (is_or, and_16_out, f7_0x00);
  and and_18 (and_18_out, is_I_arith_ins, f3_0x6);
  buf and_19 (is_ori, and_18_out);  // AND_Gate
  and and_20 (is_xor, and_1_out, f7_0x00);
  and and_21 (is_srl, and_3_out, f7_0x00);
  and and_22 (is_srai, and_4_out, f7_0x20);
  and and_23 (is_sll, and_5_out, f7_0x00);
  and and_24 (is_slt, and_6_out, f7_0x00);
  and and_25 (is_divu, and_8_out, f7_0x01);
  and and_26 (is_remu, and_9_out, f7_0x01);
  Multiplexer #(.width(4), .enable("false")) multiplexer_9 (.in1(4'b0000), .out(alu_sel), .sel(or_1_out));  // open: in0
  or or_1 (or_1_out, is_add, is_addi);
  Multiplexer #(.width(4), .enable("false")) multiplexer_10 (
    .in1(4'b0001), .out(alu_sel), .sel(or_2_out));  // open: in0
  or or_2 (or_2_out, is_and, is_andi);
  Multiplexer #(.width(4), .enable("false")) multiplexer_11 (
    .in1(4'b0010), .out(alu_sel), .sel(or_3_out));  // open: in0
  or or_3 (or_3_out, is_or, is_ori);
  Multiplexer #(.width(4), .enable("false")) multiplexer_12 (
    .in1(4'b0011), .out(alu_sel), .sel(or_4_out));  // open: in0
  or or_4 (or_4_out, is_xor, is_xori);
  Multiplexer #(.width(4), .enable("false")) multiplexer_13 (.in1(4'b0100), .out(alu_sel), .sel(is_srl));  // open: in0
  Multiplexer #(.width(4), .enable("false")) multiplexer_14 (.in1(4'b0101), .out(alu_sel), .sel(is_srai));  // open: in0
  Multiplexer #(.width(4), .enable("false")) multiplexer_15 (.in1(4'b0110), .out(alu_sel), .sel(is_sll));  // open: in0
  Multiplexer #(.width(4), .enable("false")) multiplexer_16 (
    .in1(4'b0111), .out(alu_sel), .sel(or_5_out));  // open: in0
  or or_5 (or_5_out, is_slt, is_slti);
  Multiplexer #(.width(4), .enable("false")) multiplexer_17 (.in1(4'b1000), .out(alu_sel), .sel(is_divu));  // open: in0
  Multiplexer #(.width(4), .enable("false")) multiplexer_18 (.in1(4'b1001), .out(alu_sel), .sel(is_remu));  // open: in0
  and and_27 (and_27_out, is_I_arith_ins, f3_0x5);
  and and_28 (and_28_out, is_I_arith_ins, f3_0x1);
  Multiplexer #(.width(4), .enable("false")) multiplexer_19 (
    .in0(4'b0000), .in1(alu_sel), .out(ALUSel), .sel(comparator_20_gt));
  Comparator #(.width(4), .mode("unsigned")) comparator_20 (
    .a(alu_sel), .b(4'b0000), .gt(comparator_20_gt));  // open: eq, lt
  and and_29 (and_29_out, is_R_type, f3_0x0);
  and and_30 (and_30_out, is_R_type, f3_0x3);
  and and_31 (and_31_out, is_R_type, f3_0x0);
  and and_32 (and_32_out, is_R_type, f3_0x1);
  and and_33 (is_srli, and_27_out, f7_0x00);
  and and_34 (is_slli, and_28_out, f7_0x00);
  and and_35 (is_mul, and_29_out, f7_0x01);
  and and_36 (is_mulhu, and_30_out, f7_0x01);
  and and_37 (is_sub, and_31_out, f7_0x20);
  and and_38 (is_mulh, and_32_out, f7_0x01);
  Multiplexer #(.width(4), .enable("false")) multiplexer_20 (.in1(4'b0110), .out(alu_sel), .sel(is_slli));  // open: in0
  Multiplexer #(.width(4), .enable("false")) multiplexer_21 (
    .in1(4'b1011), .out(alu_sel), .sel(is_mulhu));  // open: in0
  Multiplexer #(.width(4), .enable("false")) multiplexer_22 (.in1(4'b1110), .out(alu_sel), .sel(is_mulh));  // open: in0
  Multiplexer #(.width(4), .enable("false")) multiplexer_23 (.in1(4'b0100), .out(alu_sel), .sel(is_srli));  // open: in0
  Multiplexer #(.width(4), .enable("false")) multiplexer_24 (.in1(4'b1010), .out(alu_sel), .sel(is_mul));  // open: in0
  Multiplexer #(.width(4), .enable("false")) multiplexer_25 (.in1(4'b1100), .out(alu_sel), .sel(is_sub));  // open: in0

  // Notes on the sheet:
  //   R-type
  //   I-type
  //   S-type
  //   B-type
  //   U-type
  //   J-type
  //   func3 possible values
  //   func7 possible values
  //   xor operation
  //   srl operation
  //   srai operation
  //   sll operation
  //   slt operation
  //   divu operation
  //   remu operation
  //   add operation
  //   and operation
  //   or operation
  //   beq, blt, bltu, bne, jal, jalr
  //   MIGHT NOT NEED
  //   srli operation
  //   slli operation
  //   mul operation
  //   mulhu operation
  //   sub operation
  //   mulh operation
endmodule

module wb_sel (
  input  [6:0] opcode,
  output [1:0] WBSel
);

  wire comparator_1_eq, comparator_2_eq, comparator_3_eq, comparator_4_eq, comparator_5_eq, not_1_out,
       not_2_out;

  Comparator #(.width(7)) comparator_1 (.a(opcode), .b(7'b1101111), .eq(comparator_1_eq));  // open: gt, lt
  Comparator #(.width(7)) comparator_2 (.a(opcode), .b(7'b1100111), .eq(comparator_2_eq));  // open: gt, lt
  Comparator #(.width(7)) comparator_3 (.a(opcode), .b(7'b1100011), .eq(comparator_3_eq));  // open: gt, lt
  Comparator #(.width(7)) comparator_4 (.a(opcode), .b(7'b0000011), .eq(comparator_4_eq));  // open: gt, lt
  Comparator #(.width(7)) comparator_5 (.a(opcode), .b(7'b0100011), .eq(comparator_5_eq));  // open: gt, lt
  not not_1 (not_1_out, comparator_4_eq);
  not not_2 (not_2_out, comparator_5_eq);
  or or_1 (WBSel[1], comparator_1_eq, comparator_2_eq, comparator_3_eq, comparator_4_eq);
  and and_1 (WBSel[0], not_1_out, not_2_out);
endmodule

module b_sel (
  input  [6:0] opcode,
  input  rs2_valid,
  output MemRW,
  output BSel
);

  wire comparator_2_eq, not_1_out, not_2_out;

  Comparator #(.width(7)) comparator_1 (.a(opcode), .b(7'b0100011), .eq(MemRW));  // open: gt, lt
  Comparator #(.width(7)) comparator_2 (.a(opcode), .b(7'b1100011), .eq(comparator_2_eq));  // open: gt, lt
  not not_1 (not_1_out, MemRW);
  not not_2 (not_2_out, comparator_2_eq);
  and and_1 (BSel, not_1_out, rs2_valid, not_2_out);
endmodule

module load_parse (
  input  [31:0] read_data,
  input  [6:0] opcode,
  input  [2:0] func3,
  output [31:0] load_output
);

  wire and_1_out, and_2_out, and_3_out, comparator_1_eq, f3_0x0, f3_0x1, f3_0x2, is_load_ins;
  wire [1:0] adder_1_out, load_sel, multiplexer_3_out, multiplexer_4_out, multiplexer_5_out;
  wire [31:0] lb_input, lh_input;

  Comparator #(.width(7)) comparator_1 (.a(opcode), .b(7'b0000011), .eq(comparator_1_eq));  // open: gt, lt
  Comparator #(.width(3)) comparator_2 (.a(func3), .b(3'b000), .eq(f3_0x0));  // open: gt, lt
  Comparator #(.width(3)) comparator_3 (.a(func3), .b(3'b001), .eq(f3_0x1));  // open: gt, lt
  Comparator #(.width(3)) comparator_4 (.a(func3), .b(3'b010), .eq(f3_0x2));  // open: gt, lt
  Multiplexer #(.enable("false")) multiplexer_1 (.in0(1'b0), .in1(1'b1), .out(is_load_ins), .sel(comparator_1_eq));
  and and_1 (and_1_out, is_load_ins, f3_0x0);
  and and_2 (and_2_out, is_load_ins, f3_0x1);
  and and_3 (and_3_out, is_load_ins, f3_0x2);
  Multiplexer #(.select(2), .width(32), .enable("false")) multiplexer_2 (
    .in0(read_data), .in1(lh_input), .in2(lb_input), .out(load_output), .sel(load_sel));  // open: in3
  Multiplexer #(.width(2), .enable("false")) multiplexer_3 (
    .in0(2'b00), .in1(2'b10), .out(multiplexer_3_out), .sel(and_1_out));
  Adder #(.width(2)) adder_1 (.a(multiplexer_3_out), .b(multiplexer_4_out), .out(adder_1_out));  // open: cin, cout
  Multiplexer #(.width(2), .enable("false")) multiplexer_4 (
    .in0(2'b00), .in1(2'b01), .out(multiplexer_4_out), .sel(and_2_out));
  Multiplexer #(.width(2), .enable("false")) multiplexer_5 (
    .in0(2'b00), .in1(2'b00), .out(multiplexer_5_out), .sel(and_3_out));
  Adder #(.width(2)) adder_2 (.a(adder_1_out), .b(multiplexer_5_out), .out(load_sel));  // open: cin, cout
  assign lh_input = read_data & 32'hffff;  // AND_Gate and_4, 32 bits wide
  assign lb_input = read_data & 32'hff;  // AND_Gate and_5, 32 bits wide

  // Notes on the sheet:
  //   I-type
  //   func3 possible values
endmodule

module a_sel (
  input  [6:0] opcode,
  output ASel
);

  wire comparator_1_eq, comparator_2_eq, comparator_3_eq, not_1_out, or_1_out;

  Comparator #(.width(7)) comparator_1 (.a(opcode), .b(7'b1101111), .eq(comparator_1_eq));  // open: gt, lt
  Comparator #(.width(7)) comparator_2 (.a(opcode), .b(7'b1100011), .eq(comparator_2_eq));  // open: gt, lt
  Comparator #(.width(7)) comparator_3 (.a(opcode), .b(7'b1100111), .eq(comparator_3_eq));  // open: gt, lt
  not not_1 (not_1_out, comparator_3_eq);
  or or_1 (or_1_out, comparator_1_eq, comparator_2_eq);
  and and_1 (ASel, or_1_out, not_1_out);
endmodule

module nop_sel (
  input  [6:0] opcode,
  input  PCSel,
  output NOPSel
);

  wire comparator_1_eq, comparator_2_eq, comparator_3_eq, or_1_out;

  Comparator #(.width(7)) comparator_1 (.a(opcode), .b(7'b1101111), .eq(comparator_1_eq));  // open: gt, lt
  Comparator #(.width(7)) comparator_2 (.a(opcode), .b(7'b1100011), .eq(comparator_2_eq));  // open: gt, lt
  Comparator #(.width(7)) comparator_3 (.a(opcode), .b(7'b1100111), .eq(comparator_3_eq));  // open: gt, lt
  or or_1 (or_1_out, comparator_1_eq, comparator_2_eq, comparator_3_eq);
  and and_1 (NOPSel, or_1_out, PCSel);
endmodule
